// Logisim project problem_2.circ as structural Verilog
module main (
  input  in_1,
  input  in_2,
  input  in_3,
  input  in_4,
  input  in_5,
  input  in_6,
  input  in_7,
  input  in_8,
  input  [2:0] in_9,
  output out_10
);

  problem2 problem2_1 (
    .a(in_1), .b(in_2), .c(in_3), .d(in_4), .e(in_5), .f(in_6), .g(in_7), .h(in_8), .ch(in_9), .Data(out_10));
endmodule

// VHDL entity problem2, as the project stores it:
library IEEE;
use IEEE.STD_LOGIC_1164.ALL;

entity problem2 is
    Port (
        a  : in  STD_LOGIC;
        b  : in  STD_LOGIC;
        c  : in  STD_LOGIC;
        d  : in  STD_LOGIC;
        e  : in  STD_LOGIC;
        f  : in  STD_LOGIC;
        g  : in  STD_LOGIC;
        h  : in  STD_LOGIC;
        ch : in  STD_LOGIC_VECTOR(2 downto 0);
        Data : out STD_LOGIC
    );
end problem2;

architecture Behavioral of problem2 is
begin
    process(a, b, c, d, e, f, g, h, ch)
    begin
        case ch is
            when "000" => Data <= a;
            when "001" => Data <= b;
            when "010" => Data <= c;
            when "011" => Data <= d;
            when "100" => Data <= e;
            when "101" => Data <= f;
            when "110" => Data <= g;
            when "111" => Data <= h;
            when others => Data <= '0';
        end case;
    end process;
end Behavioral;
