// Logisim project problem_3.circ as structural Verilog
module main (
  input  [2:0] in_1
);

  wire [6:0] problem3_1_seg;

  _7_Segment_Display u_7_segment_display_1 (
    .g(problem3_1_seg[0]), .f(problem3_1_seg[1]), .a(problem3_1_seg[6]), .b(problem3_1_seg[5]),
    .e(problem3_1_seg[2]), .d(problem3_1_seg[3]), .c(problem3_1_seg[4]));  // open: dp
  problem3 problem3_1 (.sel(in_1), .seg(problem3_1_seg));
endmodule

// VHDL entity problem3, as the project stores it:
library IEEE;
use IEEE.STD_LOGIC_1164.ALL;

entity problem3 is
    Port (
        sel : in  STD_LOGIC_VECTOR(2 downto 0);
        seg : out STD_LOGIC_VECTOR(6 downto 0)
    );
end problem3;

architecture Behavioral of problem3 is
begin
    process(sel)
    begin
        case sel is
            when "000" => seg <= "1110111"; -- a
            when "001" => seg <= "0011111"; -- b
            when "010" => seg <= "0001101"; -- c
            when "011" => seg <= "0111101"; -- d
            when "100" => seg <= "1000111"; -- f
            when "101" => seg <= "1111011"; -- g
            when others => seg <= "0000000";
        end case;
    end process;
end Behavioral;
