// Logisim project problem_4.circ as structural Verilog
module main (
  output out_1
);

  wire [24:0] dipswitch_1_sw25;

  DipSwitch #(.number(25)) dipswitch_1 (
    .sw1(dipswitch_1_sw25[24]), .sw2(dipswitch_1_sw25[23]), .sw3(dipswitch_1_sw25[22]),
    .sw4(dipswitch_1_sw25[21]), .sw5(dipswitch_1_sw25[20]), .sw6(dipswitch_1_sw25[19]),
    .sw7(dipswitch_1_sw25[18]), .sw8(dipswitch_1_sw25[17]), .sw9(dipswitch_1_sw25[16]),
    .sw10(dipswitch_1_sw25[15]), .sw11(dipswitch_1_sw25[14]), .sw12(dipswitch_1_sw25[13]),
    .sw13(dipswitch_1_sw25[12]), .sw14(dipswitch_1_sw25[11]), .sw15(dipswitch_1_sw25[10]),
    .sw16(dipswitch_1_sw25[9]), .sw17(dipswitch_1_sw25[8]), .sw18(dipswitch_1_sw25[7]),
    .sw19(dipswitch_1_sw25[6]), .sw20(dipswitch_1_sw25[5]), .sw21(dipswitch_1_sw25[4]),
    .sw22(dipswitch_1_sw25[3]), .sw23(dipswitch_1_sw25[2]), .sw24(dipswitch_1_sw25[1]),
    .sw25(dipswitch_1_sw25[0]));
  problem4 problem4_1 (.vt(dipswitch_1_sw25), .result(out_1));
endmodule

// VHDL entity problem4, as the project stores it:
library IEEE;
use IEEE.STD_LOGIC_1164.ALL;

entity problem4 is
    Port (
        vt     : in  STD_LOGIC_VECTOR(24 downto 0);
        result : out STD_LOGIC
    );
end problem4;

architecture Behavioral of problem4 is
begin
    process(vt)
        variable count_ones : integer range 0 to 25;
    begin
        count_ones := 0;

        for i in 0 to 24 loop
            if vt(i) = '1' then
                count_ones := count_ones + 1;
            end if;
        end loop;

        if count_ones >= 13 then
            result <= '1';
        else
            result <= '0';
        end if;
    end process;
end Behavioral;
