// Logisim project AsyncSetClear.circ as structural Verilog
module main (
  input  in_1,
  input  in_2,
  input  in_3,
  input  in_4,
  output out_5,
  output out_6
);

  wire nand_1_out, nand_2_out, nand_3_out, nand_4_out, nand_5_out, nand_6_out, not_1_out, not_2_out;

  not not_1 (not_1_out, in_2);
  nand nand_1 (nand_1_out, in_2, in_3);
  nand nand_2 (nand_2_out, in_3, not_1_out);
  nand nand_3 (nand_3_out, nand_4_out, nand_2_out, in_4);
  not not_2 (not_2_out, in_3);
  nand nand_4 (nand_4_out, in_1, nand_1_out, nand_3_out);
  nand nand_5 (nand_5_out, nand_4_out, not_2_out);
  nand nand_6 (nand_6_out, not_2_out, nand_3_out);
  nand nand_7 (out_5, in_1, nand_5_out, out_6);
  nand nand_8 (out_6, out_5, nand_6_out, in_4);
endmodule

// VHDL entity Async_Set_Clear, as the project stores it:
library IEEE;
use IEEE.STD_LOGIC_1164.ALL;

entity DFF_Async is
    Port (
        D   : in STD_LOGIC;
        clk : in STD_LOGIC;
        set : in STD_LOGIC;
        clr : in STD_LOGIC;
        Q   : out STD_LOGIC
    );
end DFF_Async;

architecture Behavioral of DFF_Async is
    signal q_internal : STD_LOGIC := '0';
begin

    process(clk, set, clr)
    begin
        if clr = '1' then
            q_internal <= '0';
        elsif set = '1' then
            q_internal <= '1';
        elsif rising_edge(clk) then
            q_internal <= D;
        end if;
    end process;

    Q <= q_internal;

end Behavioral;
