// Logisim project DFlipFlop.circ as structural Verilog
module main (
  input  in_1,
  input  in_2,
  output out_3,
  output out_4
);

  wire nand_1_out, nand_2_out, not_1_out;

  not not_1 (not_1_out, in_1);
  nand nand_1 (nand_1_out, not_1_out, in_2);
  nand nand_2 (nand_2_out, in_1, in_2);
  nand nand_3 (out_3, nand_2_out, out_4);
  nand nand_4 (out_4, out_3, nand_1_out);
endmodule

// VHDL entity D_FlipFlop, as the project stores it:
library IEEE;
use IEEE.STD_LOGIC_1164.ALL;

entity D_Flip_Flop is
    Port (
        D   : in STD_LOGIC;
        CLK : in STD_LOGIC;
        Q   : out STD_LOGIC
    );
end D_Flip_Flop;

architecture Behavioral of D_Flip_Flop is
    signal q_internal : STD_LOGIC := '0';
begin

    process(CLK)
    begin
        if rising_edge(CLK) then
            q_internal <= D;
        end if;
    end process;

    Q <= q_internal;

end Behavioral;

// VHDL entity D_Latch, as the project stores it:
library IEEE;
use IEEE.STD_LOGIC_1164.ALL;

entity D_Latch is
    Port (
        D  : in STD_LOGIC;
        en : in STD_LOGIC;
        Q  : out STD_LOGIC
    );
end D_Latch;

architecture Behavioral of D_Latch is
    signal q_internal : STD_LOGIC := '0';
begin

    process(D, en)
    begin
        if en = '1' then
            q_internal <= D;
        end if;
    end process;

    Q <= q_internal;

end Behavioral;
