// Logisim project JKFlipFlop.circ as structural Verilog
module main (
  input  in_1,
  input  in_2,
  input  in_3,
  input  CLR_2,
  input  CLR_1,
  output out_6,
  output out_7
);

  wire nand_1_out, nand_2_out, nand_3_out, nand_4_out, nand_5_out, nand_6_out, not_1_out;

  nand nand_1 (nand_1_out, out_7, in_1, in_2);
  nand nand_2 (nand_2_out, in_2, in_3, out_6);
  not not_1 (not_1_out, in_2);
  nand nand_3 (nand_3_out, nand_1_out, nand_4_out);
  nand nand_4 (nand_4_out, nand_3_out, CLR_1, nand_2_out);
  nand nand_5 (nand_5_out, nand_3_out, not_1_out);
  nand nand_6 (nand_6_out, nand_4_out, not_1_out);
  nand nand_7 (out_6, nand_5_out, out_7);
  nand nand_8 (out_7, out_6, CLR_2, nand_6_out);
endmodule

// VHDL entity JK_FlipFlop, as the project stores it:
library IEEE;
use IEEE.STD_LOGIC_1164.ALL;

entity JK_FlipFlop is
    Port (
        J   : in STD_LOGIC;
        K   : in STD_LOGIC;
        clk : in STD_LOGIC;
        Q   : out STD_LOGIC
    );
end JK_FlipFlop;

architecture Behavioral of JK_FlipFlop is
    signal q_int : STD_LOGIC := '0';
begin

    process(clk)
    begin
        if rising_edge(clk) then
            if J = '0' and K = '0' then
                q_int <= q_int;
            elsif J = '0' and K = '1' then
                q_int <= '0';
            elsif J = '1' and K = '0' then
                q_int <= '1';
            else
                q_int <= not q_int;
            end if;
        end if;
    end process;

    Q <= q_int;

end Behavioral;
